# Fritzing sketch tuxdroid (saved by Fritzing 0.9.3b)
stripboards: 6
breadboards: 1

parts:
  U1 = L9110 H-bridge module [part_number="L9110 H-bridge"]
  Raspberry_Pi_1 = Raspberry Pi 3 [part_number=RPI-3-V1.2]  # not connected
  Part1 = Adafruit T-Cobbler Plus [part_number="Adafruit #1989 and #2028"]
  M1 = DC Motor
  M2 = DC Motor
  S1 = Pushbutton [package=THT]
  S2 = Pushbutton [package=THT]
  S3 = Pushbutton [package=THT]
  S4 = Tilt Switch [package=THT]
  LED2 = LED - 5mm [color="Red (633nm)" package="5 mm [THT]"]
  S5 = Tilt Switch [package=THT]
  S6 = Tilt Switch [package=THT]
  S7 = Tilt Switch [package=THT]
  S8 = Tilt Switch [package=THT]
  LED1 = LED - 5mm [color="Red (633nm)" package="5 mm [THT]"]

nets:
  N1: U1.B-IA, Part1.GPIO19
  N2: U1.B-IB, Part1.GPIO13
  GND: U1.GND, Part1.GND, S1.leg1, S2.leg0, S3.leg0, S4.Pin_2, LED2.cathode, S5.Pin_2, S6.Pin_2, S7.Pin_2, S8.Pin_2, LED1.cathode
  VCC: U1.VCC, Part1.+5V
  N3: U1.A-IA, Part1.GPIO25
  N4: U1.A-IB, Part1.GPIO16
  N5: U1.MOTOR_A-A, M1.pin_2
  N6: U1.MOTOR_A-B, M1.pin_1
  N7: U1.MOTOR_B-A, M2.pin_2
  N8: U1.MOTOR_B-B, M2.pin_1
  N9: Part1.GPIO5, S3.leg1
  N10: Part1.GPIO6, S2.leg1
  N11: Part1.GPIO26, S4.Pin_1
  N12: Part1.GPIO23, LED2.anode
  N13: Part1.GPIO24, LED1.anode
  N14: Part1.CE0, S5.Pin_1
  N15: Part1.CE1, S8.Pin_1
  N16: Part1.GPIO12, S1.leg0
  N17: Part1.GPIO20, S7.Pin_1
  N18: Part1.GPIO21, S6.Pin_1

notes:
  - Y/W
  Left wings
  button
  - O/B
  Right wings
  button
  - R/B
  Wings move
  sensor
  * R/W
  IR Receiver
  * Black
  Ground for led
  * Blue
  IR Transmetter
  * G
  Left eye Led
  * Y
  Right eye Led
  * O
  Light sensor
  * Gy/Br
  head button
  * R/W
  Eyes open
  sensor
  * O/B
  Eyes close
  sensor
  * Y/G
  Mouth open
  sensor
  * G/B
  Mouth close
  sensor
  * B/R
  Microphone
  * R/W
  Eyes/Mouth Motor
  * B/R
  Wings Motor

custom parts:
  Adafruit T-Cobbler Plus: The Raspberry Pi has landed on the Maker World like a 40-GPIO pinned, quad-USB ported, credit card sized bomb of DIY joy. And while you can use most of our great Model B accessories by hooking up our downgrade cable, its probably a good time to upgrade your set up and accessorize using all of the 40 pins. That's why we now carry the Assembled Adafruit Pi T-Cobbler Plus - Breakout + Cable for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
